# Fritzing sketch VR_Thermal_Glove (saved by Fritzing 0.9.3b)
breadboards: 1

parts:
  U1 = ESP32-38PinWide [part_number=ESP32-38PinWide]
  M1 = L293D Motor Driver
  M2 = L293D Motor Driver
  M3 = L293D Motor Driver
  J2 = Peltier Element
  J3 = Peltier Element
  J4 = Peltier Element
  J5 = Peltier Element
  J1 = Peltier Element
  VCC1 = 4 x AAA Battery Mount  # not connected

nets:
  N1: U1.GPIO25, M1.pin_8
  N2: U1.GPIO26, M1.pin_7
  N3: U1.GPIO27, M1.pin_6
  N4: U1.GPIO14, M1.pin_5
  N5: U1.GPIO12, M2.pin_8
  N6: U1.GND, M2.pin_7
  N7: U1.GPIO13, M2.pin_6
  N8: U1.GPIO9, M2.pin_5
  N9: U1.GPIO11, M1.pin_4, M2.pin_4, M3.pin_4
  N10: U1.GPIO6, M1.pin_3, M2.pin_3, M3.pin_3
  N11: U1.GPIO5, M3.pin_5
  N12: U1.GPIO18, M3.pin_6
  N13: M1.pin_9, J3.pin1
  N14: M1.pin_10, J3.pin2
  N15: M1.pin_11, J4.pin1
  N16: M1.pin_12, J4.pin2
  N17: M2.pin_9, J1.pin1
  N18: M2.pin_10, J1.pin2
  N19: M2.pin_11, J2.pin1
  N20: M2.pin_12, J2.pin2
  N21: M3.pin_9, J5.pin1
  N22: M3.pin_10, J5.pin2

custom parts:
  ESP32-38PinWide: Generic 38-Pin ESP32 with wide format (only access to one side of pins on a breadboard) based on Stephen Lilley's HiLetgo ESP-WROOM-32 ESP32 ESP-32S Development Board.
